# Fritzing sketch Projeto1 (saved by Fritzing 0.9.3b)
breadboards: 1

parts:
  Componente1 = Arduino Mega 2560 (Rev3)
  U1 = LCD-16X2 [package=lcd-16x2]  # not connected
  R1 = Rotary Potentiometer (Large) [maximum_resistance=10kΩ package=THT]
  R2 = Rotary Potentiometer (Large) [maximum_resistance=100kΩ package=THT]
  J1 = Piezo Speaker
  LED1 = LED - 3mm [color="Red (633nm)" package="3 mm [THT]"]  # not connected
  R3 = Resistor [tolerance=±5% resistance=10k package="0402 [SMD]"]
  M1 = DC Motor
  S1 = Momentary Switch [package=ksa_sealed_tac_switch]
  S2 = Momentary Switch [package=ksa_sealed_tac_switch]
  R4 = Resistor [tolerance=±5% resistance=10k package="2010 [SMD]"]
  R5 = Resistor [tolerance=±5% resistance=10k package="2010 [SMD]"]

nets:
  N1: Componente1.A0, R1.wiper
  N2: Componente1.A1, R2.wiper
  N3: Componente1.D12_PWM, S2.4
  N4: Componente1.D11_PWM, J1.pin2
  N5: Componente1.D10_PWM, R3.Pin_0
  N6: Componente1.5V, R1.leg1, R2.leg1, S1.1, S2.1
  N7: Componente1.GND, R1.leg2, R2.leg2, J1.pin1, M1.pin_2, R4.Pin_0, R5.Pin_0
  N8: Componente1.D6_PWM, M1.pin_1
  N9: Componente1.D7_PWM, S1.4
  N10: S1.3, R4.Pin_1
  N11: S2.3, R5.Pin_1
